# Fritzing sketch robot-seguidor-luz (saved by Fritzing 0.9.10b)
breadboards: 1

parts:
  Q2 = NPN-Transistor [part_number=TIP41 package="TO92 [THT]"]
  Q4 = NPN-Transistor [part_number=BC548 package="TO92 [THT]"]
  R1 = Resistor [tolerance=±5% power=0.25 resistance=1k package=THT]
  R2 = Resistor [tolerance=±5% power=0.25 resistance=220 package=THT]
  R3 = Resistor [tolerance=±5% power=0.25 resistance=1k package=THT]
  R4 = Resistor [tolerance=±5% power=0.25 resistance=10k package=THT]
  R5 = Resistor [tolerance=±5% power=0.25 resistance=220 package=THT]
  R6 = Resistor [tolerance=±5% power=0.25 resistance=1k package=THT]
  R7 = Resistor [tolerance=±5% power=0.25 resistance=1k package=THT]
  R8 = Resistor [tolerance=±5% power=0.25 resistance=10k package=THT]
  LED1 = LED - 5mm [color="Red (633nm)" current=0.030 package="5 mm [THT]"]
  LED2 = LED - 5mm [color="Green (570nm)" current=0.030 package="5 mm [THT]"]
  R9 = Photocell (LDR) [package=THT]
  R10 = Photocell (LDR) [package=THT]
  M3 = gear-motor
  M4 = gear-motor
  VCC1 = Battery block 9V
  Q1 = NPN-Transistor [part_number=TIP41 package="TO92 [THT]"]
  Q3 = NPN-Transistor [part_number=BC548 package="TO92 [THT]"]

nets (from the schematic view):
  GND: Q2.E, R4.Pin_0, R8.Pin_1, LED1.cathode, LED2.cathode, VCC1.-, Q1.E
  N1: Q2.B, R6.Pin_1
  N2: Q2.C, M4.pin_1
  N3: Q4.E, R5.Pin_0, R6.Pin_0
  N4: Q4.B, R7.Pin_1
  N5: Q4.C, R9.pin_1, R10.pin_0, M3.pin_1, M4.pin_2, VCC1.+, Q3.C
  N6: R1.Pin_0, R2.Pin_0, Q3.E
  N7: R1.Pin_1, Q1.B
  N8: R2.Pin_1, LED2.anode
  N9: R3.Pin_0, R4.Pin_1, R10.pin_1
  N10: R3.Pin_1, Q3.B
  N11: R5.Pin_1, LED1.anode
  N12: R7.Pin_0, R8.Pin_0, R9.pin_0
  N13: M3.pin_2, Q1.C

notes:
  Micro Robot Movil Seguidor de Luz
